# Fritzing sketch ard_proje_rfid (saved by Fritzing 0.9.3b)
breadboards: 1

parts:
  Parça1 = Arduino Uno (Rev3)
  Parça2 = RFID USB Reader
  J1 = Piezo Speaker
  S2 = Pushbutton [package="[THT]"]
  J2 = Piezo Speaker
  R1 = Resistor [tolerance=±5% resistance=220 package="2512 [SMD]"]
  R2 = Resistor [tolerance=±5% resistance=1 package="2512 [SMD]"]
  R3 = Resistor [tolerance=±5% resistance=1 package="2512 [SMD]"]

nets:
  N1: Parça1.D9_PWM, Parça2.GND
  N2: Parça1.D10_PWM/SS, Parça2.GNDT
  N3: Parça1.D11_PWM/MOSI, Parça2.ANT2
  N4: Parça1.D12/MISO, Parça2.ANT1
  N5: Parça1.D13/SCK, Parça2.CP
  N6: Parça1.D2, J2.pin2
  N7: Parça1.D3_PWM, S2.Pin_1, S2.Pin_2, R1.Pin_0
  N8: Parça1.D4, J1.pin2
  3V3: Parça1.3V3, Parça2.VCC
  N9: Parça1.5V, S2.Pin_3, S2.Pin_4
  N10: Parça1.GND, Parça2.TX-O, R1.Pin_1, R2.Pin_0, R3.Pin_0
  N11: J1.pin1, R2.Pin_1
  N12: J2.pin1, R3.Pin_1
